# Fritzing sketch door-sensor (saved by Fritzing 0.9.10b)
circuit board: 9.4cm x 4.5cm
breadboards: 1

parts:
  IC1 = AE-TYBLE16 (300mil) [part_number=K-12339 package="DIP (Dual Inline) [THT]"]
  C1 = Capacitor Polarized [package=cpol-radial-100uf-25v]
  Q1 = LTR-301 [package=ltr-301]
  R1 = Resistor [tolerance=±5% power=0.25W resistance=1k package=THT]
  S2 = Toggle Switch [package=THT]
  S1 = Reed switch [package=THT]
  R2 = Resistor [tolerance=±5% power=0.25W resistance=1 package=THT]
  J1 = female pin header, 6 pins [form="♀ (female)"]
  J2 = female pin header, 2 pins [form="♀ (female)"]
  J3 = female pin header, 2 pins [form="♀ (female)"]
  J4 = female pin header, 2 pins [form="♀ (female)"]
  IC2 = IC, DIP package, 6 pins [chip_label=R3111N211A]
  LED1 = LED - 3mm [color="Red (633nm)" current=30mA package="3 mm [THT]"]
  R3 = Resistor [tolerance=±5% power=0.25W resistance=47 package=THT]
  R4 = Resistor [tolerance=±5% power=0.25W resistance=47 package=THT]
  S3 = Toggle Switch [package=THT]
  S5 = Toggle Switch [package=THT]
  S4 = Toggle Switch [package=THT]
  BAT1 = Battery Holders [package=battcon_245mm]
  LED2 = LED - 3mm [color="Green (565nm)" current=30mA package="3 mm [THT]"]

nets:
  N1: IC1.DIP2, J1.pin2
  N2: IC1.DIP3, J1.pin3
  N3: IC1.DIP5, J1.pin5
  N4: IC1.DIP6, J1.pin6
  N5: IC1.DIP9, Q1.E, R1.Pin_0
  N6: IC1.DIP10, R4.Pin_0
  N7: IC1.DIP13, C1.-, R1.Pin_1, J1.pin4, J2.pin2, IC2.pin3, BAT1.-, LED2.cathode
  N8: IC1.DIP14, C1.+, S2.L1, S2.COM, R2.Pin_0, J1.pin1, J4.pin2, IC2.pin2, LED1.anode, S5.L1, S5.COM
  N9: Q1.C, S2.L2
  N10: S1.pin_1, J3.pin1, S3.COM, S4.L2
  N11: S1.pin_2, R2.Pin_1, J3.pin2, J4.pin1, S5.L2, S4.L1, S4.COM
  N12: J2.pin1, S3.L1
  N13: IC2.pin1, R3.Pin_1
  N14: LED1.cathode, R3.Pin_0
  N15: R4.Pin_1, LED2.anode
  N16: S3.L2, BAT1.+

custom parts:
  AE-TYBLE16 (300mil): AE-TYBLE16 BLE module whose MPU core is nRF51822 as 300mil (7.62mm) breadfriendly width, actual width is 8.0mm
